// Logisim project CheckSum.circ as structural Verilog: 1 circuit, main circuit main
module main (
  input  [7:0] in_1,
  input  [7:0] in_2,
  input  [7:0] in_3,
  output [7:0] _1_s_Complement,
  output [7:0] out_5,
  output [7:0] out_6,
  output [7:0] _1_prime_Complement,
  output [7:0] out_8
);

  wire adder_1_cout, adder_2_cout, not_1_out;
  wire [7:0] adder_2_out, adder_4_out, multiplexer_1_out, multiplexer_2_out;

  Adder adder_1 (.a(in_2), .b(in_3), .out(out_5), .cout(adder_1_cout));  // open: cin
  not not_1 (not_1_out, adder_1_cout);
  Adder adder_2 (.a(in_2), .b(in_3), .out(adder_2_out), .cout(adder_2_cout));  // open: cin
  Multiplexer #(.width(8)) multiplexer_1 (
    .in0(out_5), .in1(out_5), .out(multiplexer_1_out), .sel(not_1_out));  // open: en
  Adder adder_3 (.a(adder_2_out), .b(_1_prime_Complement), .out(out_8), .cin(adder_2_cout));  // open: cout
  assign out_6 = ~multiplexer_1_out;  // NOT_Gate not_2, 8 bits wide
  Adder adder_4 (.a(multiplexer_1_out), .b(in_1), .out(adder_4_out));  // open: cin, cout
  assign _1_s_Complement = ~adder_4_out;  // NOT_Gate not_3, 8 bits wide
  assign _1_prime_Complement = ~multiplexer_2_out;  // NOT_Gate not_4, 8 bits wide
  Multiplexer #(.width(8)) multiplexer_2 (
    .in0(adder_4_out), .in1(multiplexer_1_out), .out(multiplexer_2_out), .sel(not_1_out));  // open: en

  // Notes on the sheet:
  //   First Input
  //   Secont Input
  //   This is input must Be 00000001
  //   Checked that data is correct
endmodule
